// Logisim project CirProy2.circ as structural Verilog: 3 circuits, main circuit Octal
module Octal (
  input  in_1,
  input  [63:0] A,
  input  [63:0] B,
  input  in_4,
  input  [63:0] C,
  input  [63:0] D,
  output [63:0] out_7,
  output [63:0] out_8,
  output out_9,
  output out_10,
  output [63:0] A_B,
  output [63:0] out_12,
  output out_13,
  output [63:0] out_14,
  output out_15,
  output out_16,
  output [63:0] C_D,
  output out_18
);

  wire undriven, undriven_2;

  Adder #(.width(64)) adder_1 (.a(A), .b(B), .out(A_B), .cin(undriven), .cout(out_13));
  Adder #(.width(64)) adder_2 (.a(C), .b(D), .out(C_D), .cin(undriven_2), .cout(out_18));
  Subtractor #(.width(64)) subtractor_1 (.a(A_B), .b(C_D), .out(out_7), .bout(out_9));  // open: bin
  Negator #(.width(64)) negator_1 (.in(out_7), .out(out_8));
  Subtractor #(.width(64)) subtractor_2 (.a(A_B), .b(C_D), .out(out_12), .bout(out_15));  // open: bin
  Negator #(.width(64)) negator_2 (.in(out_12), .out(out_14));

  assign out_10 = out_9;
  assign out_16 = out_15;

  // Notes on the sheet:
  //   (A+B)-C POSITIVO
  //   (A+B)-C NEGATIVO
  //   (A+B)-(C+D) POSITIVO
  //   (A+B)-(C+D) NEGATIVO
endmodule

module Hexadecimal (
  input  in_1,
  input  [63:0] A,
  input  [63:0] B,
  input  in_4,
  input  [63:0] C,
  input  [63:0] D,
  output [63:0] out_7,
  output [63:0] out_8,
  output out_9,
  output out_10,
  output [63:0] A_B,
  output [63:0] out_12,
  output out_13,
  output [63:0] out_14,
  output out_15,
  output out_16,
  output [63:0] C_D,
  output out_18
);

  wire undriven, undriven_2;

  Adder #(.width(64)) adder_1 (.a(A), .b(B), .out(A_B), .cin(undriven), .cout(out_13));
  Adder #(.width(64)) adder_2 (.a(C), .b(D), .out(C_D), .cin(undriven_2), .cout(out_18));
  Subtractor #(.width(64)) subtractor_1 (.a(A_B), .b(C), .out(out_7), .bout(out_9));  // open: bin
  Negator #(.width(64)) negator_1 (.in(out_7), .out(out_8));
  Subtractor #(.width(64)) subtractor_2 (.a(A_B), .b(C_D), .out(out_12), .bout(out_15));  // open: bin
  Negator #(.width(64)) negator_2 (.in(out_12), .out(out_14));

  assign out_10 = out_9;
  assign out_16 = out_15;

  // Notes on the sheet:
  //   (A+B)-C POSITIVO
  //   (A+B)-C NEGATIVO
  //   (A+B)-(C+D) POSITIVO
  //   (A+B)-(C+D) NEGATIVO
endmodule

module Binario (
  input  in_1,
  input  [23:0] in_2,
  input  [23:0] in_3,
  input  in_4,
  input  [23:0] in_5,
  input  [23:0] in_6,
  output [23:0] out_7,
  output out_8,
  output [23:0] out_9,
  output out_10,
  output [23:0] out_11,
  output [23:0] out_12,
  output out_13,
  output [23:0] out_14,
  output out_15,
  output out_16,
  output [23:0] out_17,
  output out_18
);

  wire undriven, undriven_2;

  Adder #(.width(24)) adder_1 (.a(in_2), .b(in_3), .out(out_11), .cin(undriven), .cout(out_13));
  Adder #(.width(24)) adder_2 (.a(in_5), .b(in_6), .out(out_17), .cin(undriven_2), .cout(out_18));
  Subtractor #(.width(24)) subtractor_1 (.a(out_11), .b(out_17), .out(out_7), .bout(out_8));  // open: bin
  Negator #(.width(24)) negator_1 (.in(out_7), .out(out_9));
  Subtractor #(.width(24)) subtractor_2 (.a(out_11), .b(out_17), .out(out_12), .bout(out_15));  // open: bin
  Negator #(.width(24)) negator_2 (.in(out_12), .out(out_14));

  assign out_10 = out_8;
  assign out_16 = out_15;

  // Notes on the sheet:
  //   A+B
  //   C+D
  //   (A+B)-C POSITIVO
  //   (A+B)-C NEGATIVO
  //   (A+B)-(C+D) POSITIVO
  //   (A+B)-(C+D) NEGATIVO
endmodule
